# Fritzing sketch wheelchairschematics (saved by Fritzing 0.9.9b)
breadboards: 1

parts:
  부품1 = Arduino Uno (Rev3)
  BAT1 = BC9VPC [package=bc9vpc]
  L298N1 = L298N DC motor driver
  M1 = DC Motor  # not connected
  M2 = DC Motor  # not connected

nets:
  GND: 부품1.GND, BAT1.V-, L298N1.GND
  VIN: 부품1.VIN, BAT1.V+, L298N1.12V

custom parts:
  L298N DC motor driver: 2x DC motor driver with 78M05 positive voltage regulator (7..35 V) L298N: max 46 V, 2 A Set 5 V Enable jumper to enable 5 V regultor (needed for the L298N) and +5 V output at screw terminal or supply external +5 V at screw terminal Set ENA and/or ENB to +5 V to enable motor permanently or supply ENA and/or ENB with PWM signal IN1 and IN2 set rotation directory for motor A (OUT1/OUT2) IN2 and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
